// Logisim project exp6-1b.circ as structural Verilog: 1 circuit, main circuit main
module main (
  input  [2:0] in_1,
  output out_2
);

  wire decoder_1_out0, decoder_1_out2, decoder_1_out3, decoder_1_out6;

  Decoder #(.select(3), .tristate("false")) decoder_1 (
    .out0(decoder_1_out0), .out2(decoder_1_out2), .out3(decoder_1_out3), .out6(decoder_1_out6), .sel(in_1));  // open: out1, out4, out5, out7
  or or_1 (out_2, decoder_1_out0, decoder_1_out2, decoder_1_out3, decoder_1_out6);

  // Notes on the sheet:
  //   Circuit 1b
  //   Experiment 6
  //   Alexander Kellermann Nieves
endmodule
