// Logisim project exp6-1c.circ as structural Verilog: 1 circuit, main circuit main
module main (
  input  in_1,
  input  in_2,
  input  in_3,
  input  in_4,
  input  in_5,
  input  in_6,
  input  in_7,
  input  in_8,
  input  [2:0] in_9,
  output out_10
);

  Multiplexer #(.select(3), .width(1)) multiplexer_1 (
    .in0(in_8), .in1(in_7), .in2(in_6), .in3(in_5), .in4(in_4), .in5(in_3), .in6(in_2), .in7(in_1),
    .out(out_10), .sel(in_9));

  // Notes on the sheet:
  //   Alexander Kellermann Nieves
  //   Experiment 6
  //   Circuit 1c
endmodule
