// Logisim project exp7-1.circ as structural Verilog: 3 circuits, main circuit 1-bit ALU
module _1_bit_ALU (
  input  add_sub,
  input  C_in,
  input  [1:0] Selects,
  input  A,
  input  B,
  input  sli,
  output R,
  output C_out,
  output FA_out
);

  wire and_1_out, or_1_out, xor_1_out;

  and and_1 (and_1_out, A, B);
  or or_1 (or_1_out, A, B);
  xor xor_1 (xor_1_out, add_sub, B);
  full_adder full_adder_1 (.A(A), .B(xor_1_out), .C_IN(C_in), .C_OUt(C_out), .SUM(FA_out));
  Multiplexer #(.select(2), .width(1)) multiplexer_1 (
    .in0(and_1_out), .in1(or_1_out), .in2(FA_out), .in3(sli), .out(R), .sel(Selects));

  // Notes on the sheet:
  //   Name:
  //   Section #
  //   Experiment #
  //   Activity #
  //   Alexander Kellermann
  //   2
  //   7
  //   1
endmodule

module _4_bit_ALU (
  input  [3:0] A,
  input  [3:0] B,
  input  Add_Sub,
  input  [1:0] Select,
  output Zero,
  output [3:0] Result,
  output Overflow
);

  wire n1_bit_alu_1_c_out, n1_bit_alu_2_c_out, n1_bit_alu_3_c_out, n1_bit_alu_4_c_out;

  _1_bit_ALU u_1_bit_alu_1 (
    .A(A[0]), .B(B[0]), .add_sub(Add_Sub), .C_in(Add_Sub), .Selects(Select), .C_out(n1_bit_alu_1_c_out),
    .R(Result[0]));  // open: sli, FA_out
  _1_bit_ALU u_1_bit_alu_2 (
    .A(A[1]), .B(B[1]), .add_sub(Add_Sub), .C_in(n1_bit_alu_1_c_out), .Selects(Select),
    .C_out(n1_bit_alu_2_c_out), .R(Result[1]));  // open: sli, FA_out
  _1_bit_ALU u_1_bit_alu_3 (
    .A(A[2]), .B(B[2]), .add_sub(Add_Sub), .C_in(n1_bit_alu_2_c_out), .Selects(Select),
    .C_out(n1_bit_alu_3_c_out), .R(Result[2]));  // open: sli, FA_out
  _1_bit_ALU u_1_bit_alu_4 (
    .A(A[3]), .B(B[3]), .add_sub(Add_Sub), .C_in(n1_bit_alu_3_c_out), .Selects(Select),
    .C_out(n1_bit_alu_4_c_out), .R(Result[3]));  // open: sli, FA_out
  nor nor_1 (Zero, Result[0], Result[1], Result[2], Result[3]);
  xor xor_1 (Overflow, n1_bit_alu_3_c_out, n1_bit_alu_4_c_out);

  // Notes on the sheet:
  //   Name:
  //   Section #
  //   Experiment #
  //   Activity #
  //   Alexander Kellermann
  //   12 am MWF
  //   7
  //   b
endmodule

module full_adder (
  input  C_IN,
  input  A,
  input  B,
  output SUM,
  output C_OUt
);

  wire and_1_out, and_2_out, xor_1_out;

  xor xor_1 (xor_1_out, A, B);
  and and_1 (and_1_out, A, B);
  xor xor_2 (SUM, xor_1_out, C_IN);
  and and_2 (and_2_out, xor_1_out, C_IN);
  or or_1 (C_OUt, and_2_out, and_1_out);

  // Notes on the sheet:
  //   Name: Alexander Kellermann
  //   Section: 12 - 1pm MWF
  //   Experiment 7
  //   Acitvity 1
endmodule
