// Logisim project exp7-1.circ as structural Verilog: 2 circuits, main circuit 1-bit ALU
module _1_bit_ALU (
  input  add_sub,
  input  C_in,
  input  [1:0] Selects,
  input  A,
  input  B,
  input  sli,
  output R,
  output C_out,
  output FA_out
);


  // Notes on the sheet:
  //   Name:
  //   Section #
  //   Experiment #
  //   Activity #
endmodule

module _4_bit_ALU (
  input  [3:0] A,
  input  [3:0] B,
  input  Add_Sub,
  input  [1:0] Select,
  output Zero,
  output [3:0] Result,
  output Overflow
);


  // Notes on the sheet:
  //   Name:
  //   Section #
  //   Experiment #
  //   Activity #
endmodule
